# Fritzing sketch hackedlights (saved by Fritzing 0.8.5b)
breadboards: 1

parts:
  Part1 = Arduino Uno (Rev3)
  CC3K1 = Adafruit CC3000 WiFi Breakout
  LED1 = LED - 5mm [color="Red (633nm)" package="5 mm [THT]"]

nets:
  N1: Part1.D10_PWM/SS, CC3K1.CS
  N2: Part1.D11_PWM/MOSI, CC3K1.MOSI
  N3: Part1.D12/MISO, CC3K1.MISO
  N4: Part1.D13/SCK, CC3K1.CLK
  GND: Part1.GND, CC3K1.GND, LED1.cathode
  N5: Part1.D2, CC3K1.IRQ
  N6: Part1.D3_PWM, LED1.anode
  N7: Part1.D5_PWM, CC3K1.VBEN
  5V: Part1.5V, CC3K1.VIN

custom parts:
  Adafruit CC3000 WiFi Breakout: CC3000 WiFi Breakout
